# Fritzing sketch cat laser (saved by Fritzing 0.9.3b)
breadboards: 1

parts:
  Bauteil1 = Arduino Uno (Rev3)
  Bauteil3 = Thumb Joystick
  J1 = Basic Servo
  J2 = Basic Servo

nets:
  N1: Bauteil1.A0, Bauteil3.HORZ
  N2: Bauteil1.A1, Bauteil3.VERT
  N3: Bauteil1.D9_PWM, J1.pulse
  N4: Bauteil1.D10_PWM/SS, J2.pulse
  VCC: Bauteil1.5V, Bauteil3.VCC, J1.vcc, J2.vcc
  GND: Bauteil1.GND, Bauteil3.GND, J1.gnd, J2.gnd
